// Logisim project Somador(A+B+C)-Kauan.circ as structural Verilog: 1 circuit, main circuit main
module main (
  input  Valor_A,
  input  in_2,
  input  Valor_B,
  input  in_4,
  input  Valor_C,
  input  in_6,
  input  in_7,
  output Resultado,
  output out_9,
  output out_10,
  output out_11
);

  wire adder_1_cout, adder_1_out, adder_2_cout, adder_2_out, adder_3_cout, adder_4_cout;

  Adder #(.width(1)) adder_1 (.a(in_2), .b(in_4), .out(adder_1_out), .cout(adder_1_cout));  // open: cin
  Adder #(.width(1)) adder_2 (.a(Valor_A), .b(Valor_B), .out(adder_2_out), .cin(adder_1_cout), .cout(adder_2_cout));
  Adder #(.width(1)) adder_3 (.a(adder_1_out), .b(in_6), .out(out_11), .cout(adder_3_cout));  // open: cin
  Adder #(.width(1)) adder_4 (.a(adder_2_out), .b(Valor_C), .out(out_10), .cin(adder_3_cout), .cout(adder_4_cout));
  Adder #(.width(1)) adder_5 (.a(adder_2_cout), .b(in_7), .out(out_9), .cin(adder_4_cout), .cout(Resultado));
endmodule
